// Logisim project computer.circ as structural Verilog: 4 circuits, main circuit main
module main (
  input  RESET
);

  wire and_1_out, clock_1_out, command_splitter_1_ai, command_splitter_1_and, command_splitter_1_ao,
       command_splitter_1_bi, command_splitter_1_ce, command_splitter_1_ci, command_splitter_1_co,
       command_splitter_1_dec, command_splitter_1_di, command_splitter_1_eo, command_splitter_1_hlt,
       command_splitter_1_ii, command_splitter_1_inc, command_splitter_1_ma, command_splitter_1_mi,
       command_splitter_1_mo, command_splitter_1_or, command_splitter_1_spo, command_splitter_1_sub,
       not_1_out, not_2_out;
  wire [2:0] counter_1_q;
  wire [7:0] controlled_buffer_1_out, controlled_buffer_2_out, controlled_buffer_3_out,
       controlled_buffer_4_out, controlled_buffer_5_out, controlled_buffer_7_out, counter_2_q, ram_1_data,
       register_1_q, register_2_q, register_3_q;
  wire [13:11] ALU_flags;
  wire [15:0] rom_2_data;
  wire [23:0] rom_1_data;

  Clock clock_1 (.out(clock_1_out));
  assign controlled_buffer_1_out = command_splitter_1_mi ? controlled_buffer_5_out : 8'bz;  // Controlled_Buffer controlled_buffer_1
  Register register_1 (.D(controlled_buffer_3_out), .en(1'b1), .Q(register_1_q), .clk(and_1_out));  // open: clr
  Counter #(.width(3), .max('h7)) counter_1 (
    .Q(counter_1_q), .clk(not_1_out), .clr(RESET));  // open: load, D, count, carry
  not not_1 (not_1_out, and_1_out);
  assign controlled_buffer_2_out = command_splitter_1_di ? controlled_buffer_5_out : 8'bz;  // Controlled_Buffer controlled_buffer_2
  not not_2 (not_2_out, command_splitter_1_hlt);
  Register register_2 (.D(controlled_buffer_4_out), .Q(register_2_q), .clk(and_1_out), .clr(RESET));  // open: en
  RAM #(.bus("separate")) ram_1 (
    .addr(register_2_q), .din(controlled_buffer_1_out), .data(ram_1_data), .str(command_splitter_1_mi),
    .sel(1'b1), .clk(and_1_out), .ld(command_splitter_1_mo));  // open: clr
  assign controlled_buffer_3_out = command_splitter_1_ii ? controlled_buffer_5_out : 8'bz;  // Controlled_Buffer controlled_buffer_3
  Register register_3 (.D(controlled_buffer_2_out), .en(1'b1), .Q(register_3_q), .clk(and_1_out), .clr(RESET));
  and and_1 (and_1_out, not_2_out, clock_1_out);
  assign controlled_buffer_4_out = command_splitter_1_ma ? controlled_buffer_5_out : 8'bz;  // Controlled_Buffer controlled_buffer_4
  assign controlled_buffer_5_out = command_splitter_1_mo ? ram_1_data : 8'bz;  // Controlled_Buffer controlled_buffer_5
  ROM #(.addrWidth(16), .dataWidth(24)) rom_1 (
    .addr({2'b00, ALU_flags, register_1_q, counter_1_q}), .data(rom_1_data), .sel(1'b1));
  ALU ALU (
    .AI__a_register_in_data(controlled_buffer_5_out), .AO__a_register_out_data(controlled_buffer_5_out),
    .EO__sum_out_data(controlled_buffer_5_out), .BI__b_register_in_data(controlled_buffer_5_out),
    .Clock(and_1_out), .FLAGS(ALU_flags), .AO__a_register_out_signal(command_splitter_1_ao),
    .EO__sum_out_signal(command_splitter_1_eo), .AI__a_register_in_signal(command_splitter_1_ai),
    .SUB__0_for_add_1_for_substract_signal(command_splitter_1_sub),
    .BI__b_register_in_signal(command_splitter_1_bi), .AND__and_out_signal(command_splitter_1_and),
    .OR__or_out_signal(command_splitter_1_or));
  SP SP (
    .out_6(controlled_buffer_5_out), .Clock(and_1_out), .Reset(RESET), .SPO(command_splitter_1_spo),
    .DEC(command_splitter_1_dec), .INC(command_splitter_1_inc));
  ROM #(.dataWidth(16)) rom_2 (.addr(register_3_q), .data(rom_2_data));  // open: sel
  assign controlled_buffer_5_out = command_splitter_1_co ? counter_2_q : 8'bz;  // Controlled_Buffer controlled_buffer_6
  assign controlled_buffer_7_out = command_splitter_1_ci ? controlled_buffer_5_out : 8'bz;  // Controlled_Buffer controlled_buffer_7
  Counter counter_2 (
    .load(command_splitter_1_ci), .D(controlled_buffer_7_out), .count(command_splitter_1_ce),
    .Q(counter_2_q), .clk(and_1_out), .clr(RESET));  // open: carry
  Command_Splitter command_splitter_1 (
    .Command(rom_1_data), .OR(command_splitter_1_or), .AND(command_splitter_1_and),
    .INC(command_splitter_1_inc), .DEC(command_splitter_1_dec), .SPO(command_splitter_1_spo),
    .AO(command_splitter_1_ao), .II(command_splitter_1_ii), .MI(command_splitter_1_mi),
    .MO(command_splitter_1_mo), .MA(command_splitter_1_ma), .SUB(command_splitter_1_sub),
    .EO(command_splitter_1_eo), .AI(command_splitter_1_ai), .BI(command_splitter_1_bi),
    .CE(command_splitter_1_ce), .CI(command_splitter_1_ci), .CO(command_splitter_1_co),
    .HLT(command_splitter_1_hlt), .DI(command_splitter_1_di));  // open: out_2, out_3, out_4, out_5, out_6
  _7_Segment_Display u_7_segment_display_1 (.g(rom_2_data[12]));  // open: f, a, b, e, d, c, dp
  Hex_Digit_Display hex_digit_display_1 (.value(rom_2_data[11:8]));  // open: dp
  Hex_Digit_Display hex_digit_display_2 (.value(rom_2_data[7:4]));  // open: dp
  Hex_Digit_Display hex_digit_display_3 (.value(rom_2_data[3:0]));  // open: dp

  // Notes on the sheet:
  //   RAM
  //   Memory Register
  //   Input Register
  //   Clock
  //   contents of rom_1 (hex, n*v repeats v):
  //   204 1410 6*0 204 1410 204 430 c0 0 0 0 204 1410 204 610 420 c0 0 0 204 1410 204 408 4*0 204 1410
  //   2001 5*0 204 1410 204 610 2800 0 0 0 204 1410 204 450 4*0 204 1410 204 610 440 0 0 0 204 1410 10 5*0
  //   204 1410 204 430 1c0 0 0 0 204 1410 204 610 420 1c0 0 0 204 1410 10 5*0 204 1410 10 5*0 204 1410
  //   c200 2800 4*0 204 1410 10440 5*0 204 1410 6*0 204 1410 6*0 204 1410 6*0 204 1410 6*0 204 1410 6*0
  //   204 1410 6*0 204 1410 6*0 204 1410 6*0 204 1410 6*0 204 1410 6*0 204 1410 6*0 204 1410 6*0 204 1410
  //   6*0 204 1410 6*0 204 1410 6*0 204 1410 6*0 204 1410 6*0 204 1410 6*0 204 1410 6*0 204 1410 6*0 204
  //   1410 6*0 204 1410 6*0 204 1410 6*0 204 1410 6*0 204 1410 6*0 204 1410 6*0 204 1410 6*0 204 1410 6*0
  //   204 1410 6*0 204 1410 6*0 204 1410 6*0 204 1410 6*0 204 1410 6*0 204 1410 6*0 204 1410 6*0 204 1410
  //   6*0 204 1410 6*0 204 1410 6*0 204 1410 6*0 204 1410 6*0 204 1410 6*0 204 1410 6*0 204 1410 6*0 204
  //   1410 6*0 204 1410 6*0 204 1410 6*0 204 1410 6*0 204 1410 6*0 204 1410 6*0 204 1410 6*0 204 1410 6*0
  //   204 1410 6*0 204 1410 6*0 204 1410 6*0 204 1410 6*0 204 1410 6*0 204 1410 6*0 204 1410 6*0 204 1410
  //   6*0 204 1410 6*0 204 1410 6*0 204 1410 6*0 204 1410 6*0 204 1410 6*0 204 1410 6*0 204 1410 6*0 204
  //   1410 6*0 204 1410 6*0 204 1410 6*0 204 1410 6*0 204 1410 6*0 204 1410 6*0 204 1410 6*0 204 1410 6*0
  //   204 1410 6*0 204 1410 6*0 204 1410 6*0 204 1410 6*0 204 1410 6*0 204 1410 6*0 204 1410 6*0 204 1410
  //   6*0 204 1410 6*0 204 1410 6*0 204 1410 6*0 204 1410 6*0 204 1410 6*0 204 1410 6*0 204 1410 6*0 204
  //   1410 6*0 204 1410 6*0 204 1410 6*0 204 1410 6*0 204 1410 6*0 204 1410 6*0 204 1410 6*0 204 1410 6*0
  //   204 1410 6*0 204 1410 6*0 204 1410 6*0 204 1410 6*0 204 1410 6*0 204 1410 6*0 204 1410 6*0 204 1410
  //   6*0 204 1410 6*0 204 1410 6*0 204 1410 6*0 204 1410 6*0 204 1410 6*0 204 1410 6*0 204 1410 6*0 204
  //   1410 6*0 204 1410 6*0 204 1410 6*0 204 1410 6*0 204 1410 6*0 204 1410 6*0 204 1410 6*0 204 1410 6*0
  //   204 1410 6*0 204 1410 6*0 204 1410 6*0 204 1410 6*0 204 1410 6*0 204 1410 6*0 204 1410 6*0 204 1410
  //   6*0 204 1410 6*0 204 1410 6*0 204 1410 6*0 204 1410 6*0 204 1410 6*0 204 1410 6*0 204 1410 6*0 204
  //   1410 6*0 204 1410 6*0 204 1410 6*0 204 1410 6*0 204 1410 6*0 204 1410 6*0 204 1410 6*0 204 1410 6*0
  //   204 1410 6*0 204 1410 6*0 204 1410 6*0 204 1410 6*0 204 1410 6*0 204 1410 6*0 204 1410 6*0 204 1410
  //   6*0 204 1410 6*0 204 1410 6*0 204 1410 6*0 204 1410 6*0 204 1410 6*0 204 1410 6*0 204 1410 6*0 204
  //   1410 6*0 204 1410 6*0 204 1410 6*0 204 1410 6*0 204 1410 6*0 204 1410 6*0 204 1410 6*0 204 1410 6*0
  //   204 1410 6*0 204 1410 6*0 204 1410 6*0 204 1410 6*0 204 1410 6*0 204 1410 6*0 204 1410 6*0 204 1410
  //   6*0 204 1410 6*0 204 1410 6*0 204 1410 6*0 204 1410 6*0 204 1410 6*0 204 1410 6*0 204 1410 6*0 204
  //   1410 6*0 204 1410 6*0 204 1410 6*0 204 1410 6*0 204 1410 6*0 204 1410 6*0 204 1410 6*0 204 1410 6*0
  //   204 1410 6*0 204 1410 6*0 204 1410 6*0 204 1410 6*0 204 1410 6*0 204 1410 6*0 204 1410 6*0 204 1410
  //   6*0 204 1410 6*0 204 1410 6*0 204 1410 6*0 204 1410 6*0 204 1410 6*0 204 1410 6*0 204 1410 6*0 204
  //   1410 6*0 204 1410 6*0 204 1410 6*0 204 1410 6*0 204 1410 6*0 204 1410 6*0 204 1410 6*0 204 1410 6*0
  //   204 1410 6*0 204 1410 6*0 204 1410 6*0 204 1410 6*0 204 1410 6*0 204 1410 6*0 204 1410 6*0 204 1410
  //   6*0 204 1410 6*0 204 1410 6*0 204 1410 6*0 204 1410 6*0 204 1410 6*0 204 1410 6*0 204 1410 6*0 204
  //   1410 6*0 204 1410 6*0 204 1410 6*0 204 1410 6*0 204 1410 6*0 204 1410 6*0 204 1410 6*0 204 1410 6*0
  //   204 1410 6*0 204 1410 6*0 204 1410 6*0 204 1410 6*0 204 1410 6*0 204 1410 2 5*0 204 1410 6*0 204
  //   1410 204 430 c0 0 0 0 204 1410 204 610 420 c0 0 0 204 1410 204 408 4*0 204 1410 2001 5*0 204 1410
  //   204 610 2800 0 0 0 204 1410 204 450 4*0 204 1410 204 610 440 0 0 0 204 1410 10 5*0 204 1410 204 430
  //   1c0 0 0 0 204 1410 204 610 420 1c0 0 0 204 1410 10 5*0 204 1410 204 408 4*0 204 1410 c200 2800 4*0
  //   204 1410 10440 5*0 204 1410 6*0 204 1410 6*0 204 1410 6*0 204 1410 6*0 204 1410 6*0 204 1410 6*0 204
  //   1410 6*0 204 1410 6*0 204 1410 6*0 204 1410 6*0 204 1410 6*0 204 1410 6*0 204 1410 6*0 204 1410 6*0
  //   204 1410 6*0 204 1410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
  //   contents of rom_2 (hex, n*v repeats v):
  //   0 1 2 3 4 5 6 7 8 9 10 11 12 13 14 15 16 17 18 19 20 21 22 23 24 25 26 27 28 29 30 31 32 33 34 35 36
  //   37 38 39 40 41 42 43 44 45 46 47 48 49 50 51 52 53 54 55 56 57 58 59 60 61 62 63 64 65 66 67 68 69
  //   70 71 72 73 74 75 76 77 78 79 80 81 82 83 84 85 86 87 88 89 90 91 92 93 94 95 96 97 98 99 100 101
  //   102 103 104 105 106 107 108 109 110 111 112 113 114 115 116 117 118 119 120 121 122 123 124 125 126
  //   127 1128 1127 1126 1125 1124 1123 1122 1121 1120 1119 1118 1117 1116 1115 1114 1113 1112 1111 1110
  //   1109 1108 1107 1106 1105 1104 1103 1102 1101 1100 1099 1098 1097 1096 1095 1094 1093 1092 1091 1090
  //   1089 1088 1087 1086 1085 1084 1083 1082 1081 1080 1079 1078 1077 1076 1075 1074 1073 1072 1071 1070
  //   1069 1068 1067 1066 1065 1064 1063 1062 1061 1060 1059 1058 1057 1056 1055 1054 1053 1052 1051 1050
  //   1049 1048 1047 1046 1045 1044 1043 1042 1041 1040 1039 1038 1037 1036 1035 1034 1033 1032 1031 1030
  //   1029 1028 1027 1026 1025 1024 1023 1022 1021 1020 1019 1018 1017 1016 1015 1014 1013 1012 1011 1010
  //   1009 1008 1007 1006 1005 1004 1003 1002 1001
  //   Program Counter
  //   AO
  //   MI
  //   II
  //   MO
  //   MA
  //   SUB
  //   EO
  //   BI
  //   CI
  //   CE
  //   AI
  //   CO
  //   DI
  //   HLT
endmodule

module ALU (
  input  [7:0] AI__a_register_in_data,
  input  AO__a_register_out_signal,
  input  EO__sum_out_signal,
  input  AI__a_register_in_signal,
  input  SUB__0_for_add_1_for_substract_signal,
  input  BI__b_register_in_signal,
  input  AND__and_out_signal,
  input  OR__or_out_signal,
  input  [7:0] BI__b_register_in_data,
  input  Clock,
  output [7:0] AO__a_register_out_data,
  output [7:0] EO__sum_out_data,
  output [2:0] FLAGS
);

  wire not_1_out;
  wire [1:0] adder_1_cout;
  wire [7:0] adder_1_out, and_1_out, controlled_buffer_3_out, controlled_buffer_4_out,
       controlled_buffer_6_out, or_1_out, register_1_q, register_3_q, subtractor_1_out;

  assign AO__a_register_out_data = AO__a_register_out_signal ? register_1_q : 8'bz;  // Controlled_Buffer controlled_buffer_1
  assign EO__sum_out_data = EO__sum_out_signal ? controlled_buffer_4_out : 8'bz;  // Controlled_Buffer controlled_buffer_2
  assign controlled_buffer_3_out = AI__a_register_in_signal ? AI__a_register_in_data : 8'bz;  // Controlled_Buffer controlled_buffer_3
  nor nor_1 (adder_1_cout[1], EO__sum_out_data[0], EO__sum_out_data[1], EO__sum_out_data[2], EO__sum_out_data[3], EO__sum_out_data[4], EO__sum_out_data[5], EO__sum_out_data[6], EO__sum_out_data[7]);
  Register register_1 (.D(controlled_buffer_3_out), .en(1'b1), .Q(register_1_q), .clk(Clock));  // open: clr
  assign controlled_buffer_4_out = not_1_out ? adder_1_out : 8'bz;  // Controlled_Buffer controlled_buffer_4
  Adder adder_1 (.a(register_1_q), .b(register_3_q), .out(adder_1_out), .cout(adder_1_cout[0]));  // open: cin
  Register #(.width(3)) register_2 (
    .D({EO__sum_out_data[7], adder_1_cout}), .en(1'b1), .Q(FLAGS), .clk(Clock));  // open: clr
  Subtractor subtractor_1 (.a(register_1_q), .b(register_3_q), .out(subtractor_1_out));  // open: bin, bout
  not not_1 (not_1_out, SUB__0_for_add_1_for_substract_signal);
  assign controlled_buffer_4_out = SUB__0_for_add_1_for_substract_signal ? subtractor_1_out : 8'bz;  // Controlled_Buffer controlled_buffer_5
  assign controlled_buffer_6_out = BI__b_register_in_signal ? BI__b_register_in_data : 8'bz;  // Controlled_Buffer controlled_buffer_6
  assign controlled_buffer_4_out = AND__and_out_signal ? and_1_out : 8'bz;  // Controlled_Buffer controlled_buffer_7
  Register register_3 (.D(controlled_buffer_6_out), .en(1'b1), .Q(register_3_q), .clk(Clock));  // open: clr
  assign and_1_out = register_1_q & register_3_q;  // AND_Gate and_1, 8 bits wide
  assign or_1_out = register_1_q | register_3_q;  // OR_Gate or_1, 8 bits wide
  assign controlled_buffer_4_out = OR__or_out_signal ? or_1_out : 8'bz;  // Controlled_Buffer controlled_buffer_8

  // Notes on the sheet:
  //   Adder
  //   CF
  //   ZF
  //   SF
  //   A Register
endmodule

module Command_Splitter (
  input  [23:0] Command,
  output out_2,
  output out_3,
  output out_4,
  output out_5,
  output out_6,
  output OR,
  output AND,
  output INC,
  output DEC,
  output SPO,
  output AO,
  output II,
  output MI,
  output MO,
  output MA,
  output SUB,
  output EO,
  output AI,
  output BI,
  output CE,
  output CI,
  output CO,
  output HLT,
  output DI
);


  assign AI = Command[6];
  assign AND = Command[17];
  assign AO = Command[13];
  assign BI = Command[5];
  assign CE = Command[4];
  assign CI = Command[3];
  assign CO = Command[2];
  assign DEC = Command[15];
  assign DI = Command[0];
  assign EO = Command[7];
  assign HLT = Command[1];
  assign II = Command[12];
  assign INC = Command[16];
  assign MA = Command[9];
  assign MI = Command[11];
  assign MO = Command[10];
  assign OR = Command[18];
  assign out_2 = Command[23];
  assign out_3 = Command[22];
  assign out_4 = Command[21];
  assign out_5 = Command[20];
  assign out_6 = Command[19];
  assign SPO = Command[14];
  assign SUB = Command[8];
endmodule

module SP (
  input  SPO,
  input  DEC,
  input  INC,
  input  Clock,
  input  Reset,
  output [7:0] out_6
);

  wire or_1_out;
  wire [7:0] adder_1_out, controlled_buffer_2_out, register_1_q, subtractor_1_out;

  assign out_6 = SPO ? register_1_q : 8'bz;  // Controlled_Buffer controlled_buffer_1
  assign controlled_buffer_2_out = Reset ? 8'hfd : 8'bz;  // Controlled_Buffer controlled_buffer_2
  assign controlled_buffer_2_out = DEC ? subtractor_1_out : 8'bz;  // Controlled_Buffer controlled_buffer_3
  assign controlled_buffer_2_out = INC ? adder_1_out : 8'bz;  // Controlled_Buffer controlled_buffer_4
  Register register_1 (.D(controlled_buffer_2_out), .en(1'b1), .Q(register_1_q), .clk(or_1_out));  // open: clr
  or or_1 (or_1_out, Clock, Reset);
  Adder adder_1 (.a(register_1_q), .b(8'h1), .out(adder_1_out));  // open: cin, cout
  Subtractor subtractor_1 (.a(register_1_q), .b(8'h1), .out(subtractor_1_out));  // open: bin, bout
endmodule
